# Fritzing sketch Wemos_D1_Mini_BME280_Sensor (saved by Fritzing 0.9.3b)

parts:
  Part1 = BME280 Breakout
  WeMos_D1_Mini1 = WeMos D1 Mini

nets:
  N1: Part1.GND, WeMos_D1_Mini1.G
  3.3V: Part1.3.3V, WeMos_D1_Mini1.3V3
  N2: Part1.SDI/SDA, WeMos_D1_Mini1.D2
  N3: Part1.SCK/SCL, WeMos_D1_Mini1.D1

// code stored in the sketch: main.ino
void setup() {
  // do your stuff, like setup WiFi
}

void loop() {

    

}
